// Logisim project andorgate.circ as structural Verilog: 1 circuit, main circuit main
module main (
  input  A,
  input  B,
  input  C,
  output A_not,
  output f,
  output B_not,
  output C_not
);

  wire and_1_out, and_2_out, and_3_out, and_4_out, and_5_out;

  not not_1 (A_not, A);
  not not_2 (B_not, B);
  not not_3 (C_not, C);
  and and_1 (and_1_out, A, B, C);
  and and_2 (and_2_out, A_not, B, C);
  and and_3 (and_3_out, A, B_not, C_not);
  and and_4 (and_4_out, A, B_not, C);
  and and_5 (and_5_out, A_not, B_not, C);
  or or_1 (f, and_1_out, and_2_out, and_3_out, and_4_out, and_5_out);
endmodule
