// Logisim project nandgate.circ as structural Verilog: 1 circuit, main circuit main
module main (
  input  A,
  input  B,
  input  C,
  output A_not,
  output B_not,
  output f,
  output C_not
);

  wire nand_4_out, nand_5_out, nand_6_out, nand_7_out, nand_8_out;

  nand nand_1 (A_not, A, A);
  nand nand_2 (B_not, B, B);
  nand nand_3 (C_not, C, C);
  nand nand_4 (nand_4_out, A, B, C);
  nand nand_5 (nand_5_out, A_not, B, C);
  nand nand_6 (nand_6_out, A, B_not, C_not);
  nand nand_7 (nand_7_out, A, B_not, C);
  nand nand_8 (nand_8_out, A_not, B_not, C);
  nand nand_9 (f, nand_4_out, nand_5_out, nand_6_out, nand_7_out, nand_8_out);
endmodule
